// Logisim project mtg48_lab5.circ as structural Verilog: 1 circuit, main circuit main
module main (
  input  [3:0] A,
  input  [3:0] B,
  input  sub
);

  wire MSBO, out, \output , SOV, UOV, xor_2_out;
  wire [2:0] O;
  wire [3:0] MO, not_1_out;

  // Probe on A
  // Probe on B
  // Probe on {MSBO, O}
  LED led_1 (.in(UOV));
  // Probe on A
  // Probe on B
  // Probe on {MSBO, O}
  LED led_2 (.in(SOV));
  Multiplexer #(.width(4)) multiplexer_1 (.in0(B), .in1(not_1_out), .out(MO), .sel(sub));  // open: en
  assign not_1_out = ~B;  // NOT_Gate not_1, 4 bits wide
  xor xor_1 (UOV, sub, out);
  xor xor_2 (xor_2_out, A[3], MO[3]);
  not not_2 (\output , xor_2_out);
  xor xor_3 (SOV, \output , MSBO);
  Adder #(.width(4)) adder_1 (.a(A), .b(MO), .out({MSBO, O}), .cin(sub), .cout(out));

  // Other names for the same wires on the sheet: MSBA = A[3]; MSBMO = MO[3]; O[3] = MSBO
endmodule
