// Logisim project mtg48_project2.circ as structural Verilog: 5 circuits, main circuit main
module main (
);

  wire ALU_imm, ALUSrc, branch, branch_pc, branch_yes, button_1_out, CK, clock_1_out, comparator_1_lt,
       comparator_2_eq, comparator_2_gt, comparator_3_eq, comparator_4_eq, DW, Halt, jr, jump, luimux,
       MemWrite, not_1_p2, or_2_out, RAM_Src, RegWrite;
  wire [1:0] branch_offset, RegDataSrc;
  wire [2:0] ALUOp, rd, rs, rt;
  wire [3:0] register_1_q_2;
  wire [11:0] PC_1, PC_out, register_1_q, target;
  wire [15:0] addy, ALUout, bit_extender_1_out, imm, multiplexer_1_out, multiplexer_2_out, multiplexer_3_out,
       multiplexer_4_out, RAM_out, REG_rs, REG_rt, rs_imm;
  wire [21:0] rom_1_data;

  Clock clock_1 (.out(clock_1_out));
  Button button_1 (.out(button_1_out));
  or or_1 (CK, clock_1_out, button_1_out);
  Hex_Digit_Display hex_digit_display_1 (.value(register_1_q_2));  // open: dp
  Hex_Digit_Display hex_digit_display_2 (.value(register_1_q[7:4]));  // open: dp
  Hex_Digit_Display hex_digit_display_3 (.value(register_1_q[11:8]));  // open: dp
  Register #(.width(16)) register_1 (.D(REG_rs), .en(DW), .Q({register_1_q_2, register_1_q}), .clk(CK));  // open: clr
  Multiplexer #(.width(16)) multiplexer_1 (
    .in0(imm), .in1({imm[7:0], REG_rs[7:0]}), .out(multiplexer_1_out), .sel(luimux));  // open: en
  Adder #(.width(16)) adder_1 (.a(REG_rs), .b(imm), .out(rs_imm));  // open: cin, cout
  Hex_Digit_Display hex_digit_display_4 (.value(register_1_q[3:0]));  // open: dp
  assign bit_extender_1_out = {{4{1'b0}}, PC_1};  // Bit_Extender bit_extender_1
  LED led_1 (.in(Halt));
  ROM #(.addrWidth(12), .dataWidth(22)) rom_1 (.addr(PC_out), .data(rom_1_data));  // open: sel
  Multiplexer #(.width(16)) multiplexer_2 (
    .in0(REG_rt), .in1(imm), .out(multiplexer_2_out), .sel(ALU_imm));  // open: en
  Multiplexer #(.select(2), .width(16)) multiplexer_3 (
    .in0(ALUout), .in1(bit_extender_1_out), .in2(multiplexer_1_out), .in3(RAM_out), .out(multiplexer_3_out),
    .sel(RegDataSrc));  // open: en
  Comparator #(.width(16)) comparator_1 (.a(REG_rs), .b(REG_rt), .lt(comparator_1_lt));  // open: gt, eq
  Comparator #(.width(16)) comparator_2 (
    .a(REG_rs), .b(REG_rt), .gt(comparator_2_gt), .eq(comparator_2_eq));  // open: lt
  Comparator #(.width(16)) comparator_3 (.a(REG_rs), .b(REG_rt), .eq(comparator_3_eq));  // open: gt, lt
  Comparator #(.width(16)) comparator_4 (.a(REG_rs), .b(REG_rt), .eq(comparator_4_eq));  // open: gt, lt
  Control control_1 (
    .ROM_output(rom_1_data), .ALU_Src_imm(ALU_imm), .rt(rt), .rd(rd), .rs(rs), .target(target),
    .lui_mux(luimux), .halt(Halt), .REG_Src(RegDataSrc), .Display_Write(DW), .ALU_Src(ALUSrc),
    .RegWE(RegWrite), .imm(imm), .ALU_Op(ALUOp), .mem_write(MemWrite), .RAM(RAM_Src), .jump(jump),
    .branch(branch), .BO(branch_offset), .jr(jr));
  Register_File register_file_1 (
    .CLK(CK), .rs(rs), .rt(rt), .rd(rd), .REG_WE(RegWrite), .REG_rd(multiplexer_3_out), .REG_rs(REG_rs),
    .REG_rt(REG_rt));
  or or_2 (or_2_out, comparator_2_gt, comparator_2_eq);
  // NOT_Gate not_1: pin names not known; wires that end beside it: comparator_4_eq, not_1_p2
  Multiplexer #(.width(16)) multiplexer_4 (
    .in0(REG_rs), .in1(multiplexer_2_out), .out(multiplexer_4_out), .sel(ALUSrc));  // open: en
  Multiplexer #(.width(16)) multiplexer_5 (.in0(ALUout), .in1(rs_imm), .out(addy), .sel(RAM_Src));  // open: en
  Multiplexer #(.select(2)) multiplexer_6 (
    .in0(comparator_1_lt), .in1(or_2_out), .in2(comparator_3_eq), .in3(not_1_p2), .out(branch_yes),
    .sel(branch_offset));  // open: en
  ALU alu_1 (.A(REG_rs), .B(multiplexer_4_out), .ALU_Op(ALUOp), .result(ALUout));
  RAM #(.addrWidth(16), .dataWidth(16), .bus("separate")) ram_1 (
    .addr(addy), .din(REG_rt), .data(RAM_out), .str(MemWrite), .clk(CK));  // open: sel, ld, clr
  PC_FSM pc_fsm_1 (
    .CK(CK), .jump(jump), .jr(jr), .branch(branch_pc), .Halt(Halt), .jump_target(target), .imm(imm),
    .REG_rs(REG_rs), .\output (PC_out), .out_10(PC_1));
  and and_1 (branch_pc, branch, branch_yes);

  // Notes on the sheet:
  //   HALT
endmodule

module ALU (
  input  [15:0] A,
  input  [15:0] B,
  input  [2:0] ALU_Op,
  output [15:0] result
);

  wire [3:0] B_3_0;
  wire [15:0] A___B, A___B_t, A___B_t_t, A_B, A_B_t, A_t, A_t_t, nB;

  Adder #(.width(16)) adder_1 (.a(A), .b(B), .out(A_B));  // open: cin, cout
  Subtractor #(.width(16)) subtractor_1 (.a(A), .b(B), .out(A_B_t));  // open: bin, bout
  assign A___B = A & B;  // AND_Gate and_1, 16 bits wide
  Bit_Extender #(.in_width(16), .out_width(4)) bit_extender_1 (.in(B), .out(B_3_0));
  assign A___B_t_t = A | B;  // OR_Gate or_1, 16 bits wide
  assign A___B_t = A ^ B;  // XOR_Gate xor_1, 16 bits wide
  // NOT_Gate #(.width(16)) not_1: pin names not known; wires that end beside it: B, nB
  Shifter #(.width(16)) shifter_1 (.in(A), .\dist (B_3_0), .out(A_t));
  Multiplexer #(.select(3), .width(16)) multiplexer_1 (
    .in0(A_B), .in1(A_B_t), .in2(A___B), .in3(A___B_t_t), .in4(A___B_t), .in5(nB), .in6(A_t), .in7(A_t_t),
    .out(result), .sel(ALU_Op));  // open: en
  Shifter #(.width(16), .shift("lr")) shifter_2 (.in(A), .\dist (B_3_0), .out(A_t_t));
endmodule

module Register_File (
  input  CLK,
  input  [2:0] rs,
  input  [2:0] rt,
  input  [2:0] rd,
  input  REG_WE,
  input  [15:0] REG_rd,
  output [15:0] REG_rs,
  output [15:0] REG_rt
);

  wire demultiplexer_1_out0, demultiplexer_1_out1, demultiplexer_1_out2, demultiplexer_1_out3,
       demultiplexer_1_out4, demultiplexer_1_out5, demultiplexer_1_out6, demultiplexer_1_out7;
  wire [15:0] r1_q, r2_q, r3_q, r4_q, r5_q, r6_q, r7_q;

  Demultiplexer #(.select(3)) demultiplexer_1 (
    .out0(demultiplexer_1_out0), .out1(demultiplexer_1_out1), .out2(demultiplexer_1_out2),
    .out3(demultiplexer_1_out3), .out4(demultiplexer_1_out4), .out5(demultiplexer_1_out5),
    .out6(demultiplexer_1_out6), .out7(demultiplexer_1_out7), .in(REG_WE), .sel(rd));  // open: en
  Register #(.width(16)) r1 (.D(REG_rd), .en(demultiplexer_1_out1), .Q(r1_q), .clk(CLK));  // open: clr
  Register #(.width(16)) r2 (.D(REG_rd), .en(demultiplexer_1_out2), .Q(r2_q), .clk(CLK));  // open: clr
  Register #(.width(16)) r3 (.D(REG_rd), .en(demultiplexer_1_out3), .Q(r3_q), .clk(CLK));  // open: clr
  Register #(.width(16)) r4 (.D(REG_rd), .en(demultiplexer_1_out4), .Q(r4_q), .clk(CLK));  // open: clr
  Register #(.width(16)) r5 (.D(REG_rd), .en(demultiplexer_1_out5), .Q(r5_q), .clk(CLK));  // open: clr
  Register #(.width(16)) r6 (.D(REG_rd), .en(demultiplexer_1_out6), .Q(r6_q), .clk(CLK));  // open: clr
  Register #(.width(16)) r7 (.D(REG_rd), .en(demultiplexer_1_out7), .Q(r7_q), .clk(CLK));  // open: clr
  Multiplexer #(.select(3), .width(16)) multiplexer_1 (
    .in0({16{1'b0}}), .in1(r1_q), .in2(r2_q), .in3(r3_q), .in4(r4_q), .in5(r5_q), .in6(r6_q), .in7(r7_q),
    .out(REG_rs), .sel(rs));  // open: en
  Multiplexer #(.select(3), .width(16)) multiplexer_2 (
    .in0({16{1'b0}}), .in1(r1_q), .in2(r2_q), .in3(r3_q), .in4(r4_q), .in5(r5_q), .in6(r6_q), .in7(r7_q),
    .out(REG_rt), .sel(rt));  // open: en
endmodule

module PC_FSM (
  input  CK,
  input  jump,
  input  jr,
  input  branch,
  input  Halt,
  input  [11:0] jump_target,
  input  [15:0] imm,
  input  [15:0] REG_rs,
  output [11:0] \output ,
  output [11:0] out_10
);

  wire not_1_p1;
  wire [11:0] branch_offset, multiplexer_1_out, multiplexer_2_out, multiplexer_3_out;

  Multiplexer #(.width(12)) multiplexer_1 (
    .in0(12'h1), .in1(branch_offset), .out(multiplexer_1_out), .sel(branch));  // open: en
  Adder #(.width(12)) adder_1 (.a(\output ), .b(multiplexer_1_out), .out(out_10));  // open: cin, cout
  Bit_Extender #(.in_width(16), .out_width(12)) bit_extender_1 (.in(imm), .out(branch_offset));
  Multiplexer #(.width(12)) multiplexer_2 (
    .in0(out_10), .in1(jump_target), .out(multiplexer_2_out), .sel(jump));  // open: en
  Multiplexer #(.width(12)) multiplexer_3 (
    .in0(multiplexer_2_out), .in1(REG_rs[11:0]), .out(multiplexer_3_out), .sel(jr));  // open: en
  // NOT_Gate not_1: pin names not known; wires that end beside it: not_1_p1, Halt
  Register #(.width(12)) PC (.D(multiplexer_3_out), .en(not_1_p1), .Q(\output ), .clk(CK));  // open: clr

  // Other names for the same wires on the sheet: JT[11:0] = jump_target; PC_1[11:0] = out_10;
  //   REG_rs__11_0[11:0] = REG_rs[11:0]
endmodule

module Control (
  input  [21:0] ROM_output,
  output ALU_Src_imm,
  output [2:0] rt,
  output [2:0] rd,
  output [2:0] rs,
  output [11:0] target,
  output lui_mux,
  output halt,
  output [1:0] REG_Src,
  output Display_Write,
  output ALU_Src,
  output RegWE,
  output [15:0] imm,
  output [2:0] ALU_Op,
  output mem_write,
  output RAM,
  output jump,
  output branch,
  output [1:0] BO,
  output jr
);

  wire add, adi, \and , ani, beq, bge, blt, bne, j, jal, ld, li, lis, mov, mov_t, \not , \or , or_6_out,
       or_7_out, or_8_out, or_9_out, or_10_out, or_11_p3, or_12_p3, or_14_out, ori, put_t, sbi, shl, shr,
       sli, sri, sub, \xor , xri;
  wire [15:0] sxt_imm, zxt_imm;

  or or_1 (jump, j, jr, jal);
  or or_2 (branch, blt, bne, beq, bge);
  or or_3 (RegWE, li, mov, lis, lui_mux, jal, ld, ALU_Src);
  or or_4 (RAM, ld, mem_write);
  Decoder #(.select(5)) decoder_1 (
    .out0(halt), .out1(put_t), .out2(li), .out3(mov_t), .out4(lis), .out5(lui_mux), .out6(mem_write),
    .out7(ld), .out8(add), .out9(sub), .out10(\and ), .out11(\or ), .out12(\xor ), .out13(\not ),
    .out14(shl), .out15(shr), .out16(adi), .out17(sbi), .out18(ani), .out19(ori), .out20(xri), .out21(sli),
    .out22(sri), .out23(j), .out24(blt), .out25(bge), .out26(beq), .out27(bne), .out28(jal), .out29(jr),
    .sel(ROM_output[21:17]));  // open: out30, out31, en
  assign zxt_imm = {{8{1'b0}}, ROM_output[7:0]};  // Bit_Extender bit_extender_1
  assign sxt_imm = {{8{ROM_output[7]}}, ROM_output[7:0]};  // Bit_Extender bit_extender_2
  or or_5 (ALU_Src, add, \and , sub, \or , \xor , \not , shl, shr, adi, sbi, ani, ori, xri, sli, sri);
  or or_6 (or_6_out, li, ani, xri, ori);
  Multiplexer #(.width(16)) multiplexer_1 (.in0(sxt_imm), .in1(zxt_imm), .out(imm), .sel(or_6_out));  // open: en
  or or_7 (or_7_out, li, lis, lui_mux);
  or or_8 (or_8_out, \and , ani);
  or or_9 (or_9_out, \xor , xri);
  or or_10 (or_10_out, sbi, sub);
  // OR_Gate or_11: pin names not known; wires that end beside it: \or , ori, or_11_p3
  // OR_Gate or_12: pin names not known; wires that end beside it: shl, sli, or_12_p3
  Priority_Encoder #(.select(2)) priority_encoder_1 (
    .in0(1'b1), .in1(bge), .in2(beq), .in3(bne), .out(BO));  // open: gs, en_out, en_in
  or or_13 (ALU_Src_imm, adi, sbi, ani, ori, xri, sri, sli);
  Priority_Encoder #(.select(2)) priority_encoder_2 (
    .in0(1'b1), .in1(jal), .in2(or_7_out), .in3(ld), .out(REG_Src));  // open: gs, en_out, en_in
  Priority_Encoder priority_encoder_3 (
    .in0(1'b1), .in1(or_10_out), .in2(or_8_out), .in3(or_11_p3), .in4(or_9_out), .in5(\not ), .in6(or_12_p3),
    .in7(or_14_out), .out(ALU_Op));  // open: en_in, gs, en_out
  or or_14 (or_14_out, sri, shr);

  assign rd = ROM_output[16:14];
  assign rs = ROM_output[13:11];
  assign rt = ROM_output[10:8];
  assign target = ROM_output[11:0];

  // Other names for the same wires on the sheet: hlt = halt; imm_t[7:0] = ROM_output[7:0]; input[21:0] = ROM_output;
  //   opcode[4:0] = ROM_output[21:17]; lui = lui_mux; new_imm[15:0] = imm; put = Display_Write; st = mem_write
endmodule
